# Fritzing sketch end-device (saved by Fritzing 0.9.3b)
breadboards: 1

parts:
  IC1 = IC, DIP package, 28 pins [chip_label="TWELITE Dip"]
  IC2 = IC, DIP package, 6 pins [chip_label=AE-XCL101]
  J1 = Basic Force Sensing Resistor (FSR) [package=THT]
  R2 = Resistor [tolerance=±5% resistance=220 package=THT]
  LED1 = LED - 5mm [color="Red (633nm)" package="5 mm [THT]"]
  BAT1 = BATTERY-2 [package=battery-aaa]
  R3 = Resistor [tolerance=±5% resistance=10k package=THT]

nets (from the schematic view):
  N1: IC1.pin1, IC1.pin13, IC1.pin26, IC2.pin6, BAT1.+2
  N2: IC1.pin15, J1.pin_1, R2.Pin_0, R3.Pin_1
  N3: IC1.pin22, IC1.pin23, IC1.pin24, IC1.pin25, IC1.pin28, IC2.pin2, J1.pin_0
  N4: IC2.pin3, IC2.pin4, BAT1.-2
  N5: R2.Pin_1, LED1.anode
  N6: LED1.cathode, R3.Pin_0
