# Fritzing sketch gateway (saved by Fritzing 0.9.3b)
breadboards: 1

parts:
  IC1 = IC, DIP package, 28 pins [chip_label="TWELITE Dip"]
  IC2 = IC, DIP package, 24 pins [chip_label=AE-UM232R]

nets:
  N1: IC1.pin3, IC2.pin1
  N2: IC1.pin10, IC2.pin5
  N3: IC1.pin13, IC1.pin14, IC2.pin7
  N4: IC1.pin22, IC1.pin23, IC1.pin24, IC1.pin25, IC1.pin28, IC2.pin19
